# Fritzing sketch espduino-pir (saved by Fritzing 0.9.6b)

parts:
  M1 = >Wemos D1 R32
  Componente1 = HC-SR501 Body Sensor Module

nets:
  5V: M1.5V, Componente1.VCC
  GND: M1.GND, Componente1.GND
  N1: M1.IO14, Componente1.OUT

custom parts:
  >Wemos D1 R32: Wemos D1 R32 - This board is used with dual-mode Wi-Fi and Bluetooth chips, which is safe, reliable, and scalable to a variety of applications. DC in 5V-12V, 1 analog input(3.2V max input), a Micro USB connection, Compatible with D1 R32=WiFi+bluetooth+UNO
  HC-SR501 Body Sensor Module: Pyroelectric Infrared PIR Motion Sensor Detector Module
